// Logisim project ex1.circ as structural Verilog: 2 circuits, main circuit full_adder
module half_adder (
  input  A,
  input  B,
  output Sum,
  output Cout
);

  wire xnor_1_out;

  xor xor_1 (Sum, A, B);
  xnor xnor_1 (xnor_1_out, A, B);
  and and_1 (Cout, xnor_1_out, B);

  // Notes on the sheet:
  //   Fixed I/O
  //   INPUTS
  //   Don't touch
  //   OUTPUTS
endmodule

module full_adder (
  input  A,
  input  B,
  input  Cin,
  output Sum,
  output Cout
);

  wire and_1_out, and_2_out, and_3_out, or_1_out, xor_1_out;

  xor xor_1 (xor_1_out, A, B);
  and and_1 (and_1_out, B, A);
  and and_2 (and_2_out, B, Cin);
  and and_3 (and_3_out, A, Cin);
  xor xor_2 (Sum, Cin, xor_1_out);
  or or_1 (or_1_out, and_1_out, and_2_out);
  or or_2 (Cout, or_1_out, and_3_out);

  // Notes on the sheet:
  //   Fixed I/O
  //   INPUTS
  //   Don't touch
  //   OUTPUTS
endmodule
