// Logisim project ex2.circ as structural Verilog: 2 circuits, main circuit Adder1
module Adder1 (
  input  [3:0] A,
  input  [3:0] B,
  output [3:0] Sum
);

  wire full_adder_1_cout, full_adder_2_cout, full_adder_3_cout;

  full_adder full_adder_1 (.A(A[0]), .B(B[0]), .Cin(1'b0), .Sum(Sum[0]), .Cout(full_adder_1_cout));
  full_adder full_adder_2 (.A(A[1]), .B(B[1]), .Cin(full_adder_1_cout), .Sum(Sum[1]), .Cout(full_adder_2_cout));
  full_adder full_adder_3 (.A(A[2]), .B(B[2]), .Cin(full_adder_2_cout), .Sum(Sum[2]), .Cout(full_adder_3_cout));
  full_adder full_adder_4 (.A(A[3]), .B(B[3]), .Cin(full_adder_3_cout), .Sum(Sum[3]));  // open: Cout

  // Notes on the sheet:
  //   Fixed I/O
  //   INPUTS
  //   Don't touch
  //   OUTPUTS
endmodule

module Subtractor1 (
  input  [3:0] A,
  input  [3:0] B,
  output [3:0] Sum
);

  wire full_adder_1_cout, full_adder_2_cout, full_adder_3_cout, not_1_out, not_2_out, not_3_out, not_4_out,
       pull_resistor_1_node;

  not not_1 (not_1_out, B[3]);
  not not_2 (not_2_out, B[2]);
  not not_3 (not_3_out, B[1]);
  not not_4 (not_4_out, B[0]);
  Pull_Resistor #(.pull(1)) pull_resistor_1 (.node(pull_resistor_1_node));
  full_adder full_adder_1 (.A(A[0]), .B(not_4_out), .Cin(pull_resistor_1_node), .Sum(Sum[0]), .Cout(full_adder_1_cout));
  full_adder full_adder_2 (.A(A[1]), .B(not_3_out), .Cin(full_adder_1_cout), .Sum(Sum[1]), .Cout(full_adder_2_cout));
  full_adder full_adder_3 (.A(A[2]), .B(not_2_out), .Cin(full_adder_2_cout), .Sum(Sum[2]), .Cout(full_adder_3_cout));
  full_adder full_adder_4 (.A(A[3]), .B(not_1_out), .Cin(full_adder_3_cout), .Sum(Sum[3]));  // open: Cout

  // Notes on the sheet:
  //   Fixed I/O
  //   INPUTS
  //   Don't touch
  //   OUTPUTS
endmodule
