// Logisim project ex3.circ as structural Verilog: 1 circuit, main circuit display_driver
module display_driver (
  input  [3:0] Input_Number,
  output [6:0] Disp
);

  wire comparator_1_eq, comparator_2_eq, comparator_3_eq, comparator_4_eq, comparator_5_eq, comparator_6_eq,
       comparator_7_eq, comparator_8_eq, comparator_9_eq, comparator_10_eq, comparator_11_eq,
       comparator_12_eq, comparator_13_eq, comparator_14_eq, comparator_15_eq, comparator_16_eq;

  Comparator #(.width(4)) comparator_1 (.a(Input_Number), .b(4'b0000), .eq(comparator_1_eq));  // open: gt, lt
  Comparator #(.width(4)) comparator_2 (.a(Input_Number), .b(4'b0001), .eq(comparator_2_eq));  // open: gt, lt
  Comparator #(.width(4)) comparator_3 (.a(Input_Number), .b(4'b0010), .eq(comparator_3_eq));  // open: gt, lt
  Comparator #(.width(4)) comparator_4 (.a(Input_Number), .b(4'b0011), .eq(comparator_4_eq));  // open: gt, lt
  Comparator #(.width(4)) comparator_5 (.a(Input_Number), .b(4'b0100), .eq(comparator_5_eq));  // open: gt, lt
  Comparator #(.width(4)) comparator_6 (.a(Input_Number), .b(4'b0101), .eq(comparator_6_eq));  // open: gt, lt
  Comparator #(.width(4)) comparator_7 (.a(Input_Number), .b(4'b0110), .eq(comparator_7_eq));  // open: gt, lt
  Comparator #(.width(4)) comparator_8 (.a(Input_Number), .b(4'b0111), .eq(comparator_8_eq));  // open: gt, lt
  Comparator #(.width(4)) comparator_9 (.a(Input_Number), .b(4'b1000), .eq(comparator_9_eq));  // open: gt, lt
  Comparator #(.width(4)) comparator_10 (.a(Input_Number), .b(4'b1001), .eq(comparator_10_eq));  // open: gt, lt
  Comparator #(.width(4)) comparator_11 (.a(Input_Number), .b(4'b1010), .eq(comparator_11_eq));  // open: gt, lt
  Comparator #(.width(4)) comparator_12 (.a(Input_Number), .b(4'b1011), .eq(comparator_12_eq));  // open: gt, lt
  Comparator #(.width(4)) comparator_13 (.a(Input_Number), .b(4'b1100), .eq(comparator_13_eq));  // open: gt, lt
  Comparator #(.width(4)) comparator_14 (.a(Input_Number), .b(4'b1101), .eq(comparator_14_eq));  // open: gt, lt
  Comparator #(.width(4)) comparator_15 (.a(Input_Number), .b(4'b1110), .eq(comparator_15_eq));  // open: gt, lt
  Comparator #(.width(4)) comparator_16 (.a(Input_Number), .b(4'b1111), .eq(comparator_16_eq));  // open: gt, lt
  or or_1 (Disp[0], comparator_3_eq, comparator_4_eq, comparator_5_eq, comparator_6_eq, comparator_7_eq, comparator_9_eq, comparator_10_eq, comparator_11_eq, comparator_12_eq, comparator_14_eq, comparator_15_eq, comparator_16_eq);
  or or_2 (Disp[1], comparator_1_eq, comparator_5_eq, comparator_6_eq, comparator_7_eq, comparator_9_eq, comparator_10_eq, comparator_11_eq, comparator_12_eq, comparator_13_eq, comparator_15_eq, comparator_16_eq);
  or or_3 (Disp[2], comparator_1_eq, comparator_3_eq, comparator_4_eq, comparator_6_eq, comparator_7_eq, comparator_8_eq, comparator_9_eq, comparator_10_eq, comparator_11_eq, comparator_13_eq, comparator_15_eq, comparator_16_eq);
  _7_Segment_Display u_7_segment_display_1 (
    .g(Disp[0]), .f(Disp[1]), .a(Disp[2]), .b(Disp[3]), .e(Disp[4]), .d(Disp[5]), .c(Disp[6]));  // open: dp
  or or_4 (Disp[3], comparator_1_eq, comparator_2_eq, comparator_3_eq, comparator_4_eq, comparator_5_eq, comparator_8_eq, comparator_9_eq, comparator_10_eq, comparator_11_eq, comparator_14_eq);
  or or_5 (Disp[4], comparator_1_eq, comparator_3_eq, comparator_7_eq, comparator_9_eq, comparator_11_eq, comparator_12_eq, comparator_13_eq, comparator_14_eq, comparator_15_eq, comparator_16_eq);
  or or_6 (Disp[5], comparator_1_eq, comparator_3_eq, comparator_4_eq, comparator_6_eq, comparator_7_eq, comparator_9_eq, comparator_10_eq, comparator_12_eq, comparator_13_eq, comparator_14_eq, comparator_15_eq);
  or or_7 (Disp[6], comparator_1_eq, comparator_2_eq, comparator_4_eq, comparator_5_eq, comparator_6_eq, comparator_7_eq, comparator_8_eq, comparator_9_eq, comparator_11_eq, comparator_12_eq, comparator_14_eq, comparator_10_eq);

  // Other names for the same wires on the sheet: Disp1 = Disp[0]; Disp2 = Disp[1]; Disp3 = Disp[2]; Disp4 = Disp[3];
  //   Disp5 = Disp[4]; Disp6 = Disp[5]; Disp7 = Disp[6]

  // Notes on the sheet:
  //   Fixed I/O
  //   INPUTS
  //   Don't touch
  //   OUTPUTS
endmodule
