// Logisim project ex1.circ as structural Verilog: 1 circuit, main circuit Multiplier1
module Multiplier1 (
  input  [3:0] A,
  input  [3:0] B,
  output [7:0] result
);

  wire a0b1, a0b2, a0b3, a1b0, a1b1, a1b2, a1b3, a2b0, a2b1, a2b2, a2b3, a3b0, a3b1, a3b2, a3b3,
       adder_1_cout, adder_2_cout, adder_2_out, adder_3_cout, adder_3_out, adder_4_cout, adder_4_out,
       adder_5_cout, adder_6_cout, adder_6_out, adder_7_cout, adder_7_out, adder_8_cout, adder_8_out,
       adder_9_cout, adder_10_cout, adder_11_cout;

  and and_1 (result[0], A[0], B[0]);
  and and_2 (a2b0, A[2], B[0]);
  and and_3 (a2b1, A[2], B[1]);
  Adder #(.width(1)) adder_1 (.a(a0b1), .b(a1b0), .out(result[1]), .cout(adder_1_cout));  // open: cin
  Adder #(.width(1)) adder_2 (.a(a1b1), .b(a2b0), .out(adder_2_out), .cin(adder_1_cout), .cout(adder_2_cout));
  Adder #(.width(1)) adder_3 (.a(a2b1), .b(a3b0), .out(adder_3_out), .cin(adder_2_cout), .cout(adder_3_cout));
  Adder #(.width(1)) adder_4 (.a(a3b1), .b(1'b0), .out(adder_4_out), .cin(adder_3_cout), .cout(adder_4_cout));
  and and_4 (a0b1, A[0], B[1]);
  and and_5 (a0b2, A[0], B[2]);
  and and_6 (a2b2, A[2], B[2]);
  and and_7 (a0b3, A[0], B[3]);
  and and_8 (a2b3, A[2], B[3]);
  Adder #(.width(1)) adder_5 (.a(adder_2_out), .b(a0b2), .out(result[2]), .cout(adder_5_cout));  // open: cin
  Adder #(.width(1)) adder_6 (.a(adder_3_out), .b(a1b2), .out(adder_6_out), .cin(adder_5_cout), .cout(adder_6_cout));
  Adder #(.width(1)) adder_7 (.a(adder_4_out), .b(a2b2), .out(adder_7_out), .cin(adder_6_cout), .cout(adder_7_cout));
  Adder #(.width(1)) adder_8 (.a(adder_4_cout), .b(a3b2), .out(adder_8_out), .cin(adder_7_cout), .cout(adder_8_cout));
  and and_9 (a1b0, A[1], B[0]);
  and and_10 (a3b0, A[3], B[0]);
  and and_11 (a3b1, A[3], B[1]);
  Adder #(.width(1)) adder_9 (.a(adder_6_out), .b(a0b3), .out(result[3]), .cout(adder_9_cout));  // open: cin
  Adder #(.width(1)) adder_10 (.a(adder_7_out), .b(a1b3), .out(result[4]), .cin(adder_9_cout), .cout(adder_10_cout));
  Adder #(.width(1)) adder_11 (.a(adder_8_out), .b(a2b3), .out(result[5]), .cin(adder_10_cout), .cout(adder_11_cout));
  Adder #(.width(1)) adder_12 (.a(adder_8_cout), .b(a3b3), .out(result[6]), .cin(adder_11_cout), .cout(result[7]));
  and and_12 (a1b1, A[1], B[1]);
  and and_13 (a1b2, A[1], B[2]);
  and and_14 (a3b2, A[3], B[2]);
  and and_15 (a1b3, A[1], B[3]);
  and and_16 (a3b3, A[3], B[3]);

  // Other names for the same wires on the sheet: a0b0 = result[0]

  // Notes on the sheet:
  //   Fixed I/O
  //   INPUTS
  //   Don't touch
  //   OUTPUTS
endmodule
